// Logisim project control-logic.circ as structural Verilog: 1 circuit, main circuit control_logic
module control_logic (
  input  [31:0] Instruction,
  input  BrEq,
  input  BrLt,
  output PCSel,
  output RegWEn,
  output [2:0] ImmSel,
  output BrUn,
  output ASel,
  output BSel,
  output [3:0] ALUSel,
  output MemWEn,
  output [1:0] WBSel
);

  wire and_1_out, and_2_out, and_3_out, and_4_out, and_5_out, and_6_out, and_7_out, and_8_out, and_9_out,
       and_10_out, and_11_out, and_12_out, and_13_out, and_14_out, and_15_out, and_16_out, and_17_out,
       and_18_out, and_19_out, and_20_out, and_21_out, and_22_out, and_23_out, and_24_out, and_25_out,
       and_26_out, and_27_out, and_28_out, and_29_out, and_30_out, and_31_out, and_32_out, and_33_out,
       and_34_out, and_35_out, and_36_out, and_37_out, and_38_out, and_39_out, and_40_out, and_41_out,
       comparator_1_eq, comparator_2_eq, comparator_3_eq, comparator_7_eq, comparator_8_eq, comparator_9_eq,
       comparator_10_eq, comparator_11_eq, comparator_12_eq, comparator_13_eq, comparator_14_eq,
       comparator_15_eq, decoder_1_out0, decoder_1_out1, decoder_1_out4, decoder_1_out5, decoder_1_out6,
       decoder_1_out7, not_1_out, not_2_out, not_3_out, s0, s1, s2, s3, s4, s5, s6, s7, t0, t1, t2;
  wire [5:0] ROMin;
  wire [15:14] rom_1_data;

  ROM #(.addrWidth(6), .dataWidth(16)) rom_1 (
    .addr(ROMin), .data({rom_1_data, WBSel, MemWEn, ALUSel, BSel, ASel, BrUn, ImmSel, RegWEn}));
  Comparator #(.width(7)) comparator_1 (.a(Instruction[6:0]), .b(7'b1100011), .eq(comparator_1_eq));  // open: gt, lt
  Decoder #(.select(3)) decoder_1 (
    .out0(decoder_1_out0), .out1(decoder_1_out1), .out4(decoder_1_out4), .out5(decoder_1_out5),
    .out6(decoder_1_out6), .out7(decoder_1_out7), .sel(Instruction[14:12]));  // open: out2, out3, en
  Comparator #(.width(7)) comparator_2 (.a(Instruction[6:0]), .b(7'b1101111), .eq(comparator_2_eq));  // open: gt, lt
  Comparator #(.width(7)) comparator_3 (.a(Instruction[6:0]), .b(7'b1100111), .eq(comparator_3_eq));  // open: gt, lt
  not not_1 (not_1_out, BrEq);
  not not_2 (not_2_out, BrLt);
  not not_3 (not_3_out, BrLt);
  and and_1 (and_1_out, comparator_1_eq, BrEq, decoder_1_out0);
  and and_2 (and_2_out, comparator_1_eq, not_1_out, decoder_1_out1);
  and and_3 (and_3_out, comparator_1_eq, BrLt, decoder_1_out4);
  and and_4 (and_4_out, comparator_1_eq, BrLt, decoder_1_out6);
  and and_5 (and_5_out, comparator_1_eq, not_2_out, decoder_1_out5);
  and and_6 (and_6_out, comparator_1_eq, not_3_out, decoder_1_out7);
  Decoder #(.select(3)) decoder_2 (
    .out0(s0), .out1(s1), .out2(s2), .out3(s3), .out4(s4), .out5(s5), .out6(s6), .out7(s7),
    .sel(Instruction[14:12]));  // open: en
  Comparator #(.mode("unsigned"), .width(7)) comparator_4 (
    .a(Instruction[31:25]), .b({7{1'b0}}), .eq(t0));  // open: gt, lt
  Comparator #(.mode("unsigned"), .width(7)) comparator_5 (
    .a(Instruction[31:25]), .b(7'b0100000), .eq(t2));  // open: gt, lt
  Comparator #(.mode("unsigned"), .width(7)) comparator_6 (
    .a(Instruction[31:25]), .b(7'b0000001), .eq(t1));  // open: gt, lt
  or or_1 (PCSel, comparator_3_eq, and_1_out, and_2_out, and_3_out, and_4_out, and_5_out, and_6_out, comparator_2_eq);
  Comparator #(.mode("unsigned"), .width(7)) comparator_7 (
    .a(Instruction[6:0]), .b(7'b0110011), .eq(comparator_7_eq));  // open: gt, lt
  Comparator #(.mode("unsigned"), .width(7)) comparator_8 (
    .a(Instruction[6:0]), .b(7'b0000011), .eq(comparator_8_eq));  // open: gt, lt
  Comparator #(.mode("unsigned"), .width(7)) comparator_9 (
    .a(Instruction[6:0]), .b(7'b0010011), .eq(comparator_9_eq));  // open: gt, lt
  Comparator #(.mode("unsigned"), .width(7)) comparator_10 (
    .a(Instruction[6:0]), .b(7'b0100011), .eq(comparator_10_eq));  // open: gt, lt
  Comparator #(.mode("unsigned"), .width(7)) comparator_11 (
    .a(Instruction[6:0]), .b(7'b1100011), .eq(comparator_11_eq));  // open: gt, lt
  Comparator #(.mode("unsigned"), .width(7)) comparator_12 (
    .a(Instruction[6:0]), .b(7'b0010111), .eq(comparator_12_eq));  // open: gt, lt
  Comparator #(.mode("unsigned"), .width(7)) comparator_13 (
    .a(Instruction[6:0]), .b(7'b0110111), .eq(comparator_13_eq));  // open: gt, lt
  Comparator #(.mode("unsigned"), .width(7)) comparator_14 (
    .a(Instruction[6:0]), .b(7'b1101111), .eq(comparator_14_eq));  // open: gt, lt
  Comparator #(.mode("unsigned"), .width(7)) comparator_15 (
    .a(Instruction[6:0]), .b(7'b1100111), .eq(comparator_15_eq));  // open: gt, lt
  and and_7 (and_7_out, comparator_7_eq, s1);
  and and_8 (and_8_out, comparator_7_eq, s0);
  and and_9 (and_9_out, and_8_out, t0);
  and and_10 (and_10_out, and_8_out, t1);
  and and_11 (and_11_out, and_8_out, t2);
  and and_12 (and_12_out, and_7_out, t0);
  and and_13 (and_13_out, and_7_out, t1);
  and and_14 (and_14_out, comparator_7_eq, t1, s1);
  and and_15 (and_15_out, comparator_7_eq, t0, s2);
  and and_16 (and_16_out, comparator_7_eq, t0, s4);
  and and_17 (and_17_out, comparator_7_eq, s5);
  and and_18 (and_18_out, comparator_7_eq, t0, s6);
  and and_19 (and_19_out, comparator_7_eq, t0, s7);
  and and_20 (and_20_out, comparator_8_eq, s0);
  and and_21 (and_21_out, comparator_8_eq, s1);
  and and_22 (and_22_out, comparator_8_eq, s2);
  and and_23 (and_23_out, comparator_9_eq, s0);
  and and_24 (and_24_out, comparator_9_eq, s1);
  and and_25 (and_25_out, comparator_9_eq, s2);
  and and_26 (and_26_out, comparator_9_eq, s4);
  and and_27 (and_27_out, comparator_9_eq, t0, s5);
  and and_28 (and_28_out, comparator_9_eq, t2, s5);
  and and_29 (and_29_out, comparator_9_eq, s6);
  and and_30 (and_30_out, comparator_9_eq, s7);
  and and_31 (and_31_out, comparator_10_eq, s0);
  and and_32 (and_32_out, comparator_10_eq, s1);
  and and_33 (and_33_out, comparator_10_eq, s2);
  and and_34 (and_34_out, comparator_11_eq, s0);
  and and_35 (and_35_out, comparator_11_eq, s1);
  and and_36 (and_36_out, comparator_11_eq, s4);
  and and_37 (and_37_out, comparator_11_eq, s5);
  and and_38 (and_38_out, comparator_11_eq, s6);
  and and_39 (and_39_out, comparator_11_eq, s7);
  and and_40 (and_40_out, t0, and_17_out);
  and and_41 (and_41_out, and_17_out, t2);
  Priority_Encoder #(.select_enc(6)) priority_encoder_1 (
    .in0(and_9_out), .in1(and_10_out), .in2(and_11_out), .in3(and_12_out), .in4(and_13_out),
    .in5(and_14_out), .in6(and_15_out), .in7(and_16_out), .in8(and_40_out), .in9(and_41_out),
    .in10(and_18_out), .in11(and_19_out), .in12(and_20_out), .in13(and_21_out), .in14(and_22_out),
    .in15(and_23_out), .in16(and_24_out), .in17(and_25_out), .in18(and_26_out), .in19(and_27_out),
    .in20(and_28_out), .in21(and_29_out), .in22(and_30_out), .in23(and_31_out), .in24(and_32_out),
    .in25(and_33_out), .in26(and_34_out), .in27(and_35_out), .in28(and_36_out), .in29(and_37_out),
    .in30(and_38_out), .in31(and_39_out), .in32(comparator_12_eq), .in33(comparator_13_eq),
    .in34(comparator_14_eq), .in35(comparator_15_eq), .out(ROMin));  // open: in36, in37, in38, in39, in40, in41, in42, in43, in44, in45, in46, in47, in48, in49, in50, in51, in52, in53, in54, in55, in56, in57, in58, in59, in60, in61, in62, in63, gs, en_out, en_in

  // Other names for the same wires on the sheet: opcode[6:0] = Instruction[6:0]; fun3[2:0] = Instruction[14:12];
  //   fun7[6:0] = Instruction[31:25]

  // Notes on the sheet:
  //   INPUTS to your circuit
  //   Connect ROM Input here ->
  //   contents of rom_1 (hex, n*v repeats v):
  //   1001 1401 1601 1081 1481 1581 1101 1201 1281 1681 1301 1381 2041 2041 2041 1041 10c1 1141 1241 12c1
  //   16c1 1341 13c1 842 842 842 4*64 74 74 1067 17c7 69 41
  //   ROM FOR CONTROL LOGIC
  //   DON'T CHANGE THE LOCATIONS OF THE INPUTS AND OUTPUTS!
  //   This is only if you choose to do the ROM option
  //   OUTPUT from your circuit
  //   Reminder: If using ROM, use combinational logic for PCSel
endmodule
