// Logisim project partial-load.circ as structural Verilog: 1 circuit, main circuit partial_load
module partial_load (
  input  [31:0] Instruction,
  input  [31:0] MemAddress,
  input  [31:0] DataFromMem,
  output [31:0] DataToReg
);

  wire [7:0] multiplexer_1_out;
  wire [15:0] multiplexer_2_out;
  wire [16:0] multiplexer_5_out;
  wire [24:0] multiplexer_4_out;
  wire [31:0] multiplexer_3_out;

  Multiplexer #(.select(2), .width(8)) multiplexer_1 (
    .in0(DataFromMem[7:0]), .in1(DataFromMem[15:8]), .in2(DataFromMem[23:16]), .in3(DataFromMem[31:24]),
    .out(multiplexer_1_out), .sel(MemAddress[1:0]));
  Multiplexer #(.select(2), .width(16)) multiplexer_2 (
    .in0(DataFromMem[15:0]), .in1(DataFromMem[23:8]), .in2(DataFromMem[31:16]), .out(multiplexer_2_out),
    .sel(MemAddress[1:0]));  // open: in3
  Multiplexer #(.select(2), .width(32)) multiplexer_3 (
    .in0(DataFromMem), .out(multiplexer_3_out), .sel(MemAddress[1:0]));  // open: in1, in2, in3
  Multiplexer #(.width(25)) multiplexer_4 (
    .in0({25{1'b0}}), .in1({25{1'b1}}), .out(multiplexer_4_out), .sel(multiplexer_1_out[7]));
  Multiplexer #(.width(17)) multiplexer_5 (
    .in0({17{1'b0}}), .in1({17{1'b1}}), .out(multiplexer_5_out), .sel(multiplexer_2_out[15]));
  Multiplexer #(.select(2), .width(32)) multiplexer_6 (
    .in0({multiplexer_4_out, multiplexer_1_out[6:0]}), .in1({multiplexer_5_out, multiplexer_2_out[14:0]}),
    .in2(multiplexer_3_out), .out(DataToReg), .sel(Instruction[13:12]));  // open: in3

  // Other names for the same wires on the sheet: opcode[6:0] = Instruction[6:0]; fun3[2:0] = Instruction[14:12]

  // Notes on the sheet:
  //   INPUTS to your circuit
  //   DON'T CHANGE THE LOCATIONS OF THE INPUTS AND OUTPUTS!
  //   OUTPUT from your circuit
endmodule
